# Fritzing sketch ModeloGeneral (saved by Fritzing 0.9.3b)
breadboards: 1

parts:
  VCC1 = 4 x AAA Battery Mount
  Componente1 = Arduino Uno (Rev3) - ICSP
  hc-sr1 = hc-sr04
  U1 = ESP8266 ESP-01 Upgraded WiFi Module [part_number=ESP8266]
  U2 = SUP500F [package=sup500f]

nets:
  GND: VCC1.-, Componente1.GND, hc-sr1.GND, U1.GND, U2.RX-I
  N1: VCC1.+, Componente1.VIN
  N2: Componente1.D2, hc-sr1.Trig
  N3: Componente1.D3_PWM, hc-sr1.Echo
  N4: Componente1.D4, U1.RXD
  N5: Componente1.D5_PWM, U1.TXD
  N6: Componente1.D6_PWM, U2.TX-O
  N7: Componente1.D7, U2.GND
  VCC: Componente1.3V3, U1.VCC, U1.CH_PD, U2.VCC
  5V: Componente1.5V, hc-sr1.VCC

custom parts:
  ESP8266 ESP-01 Upgraded WiFi Module: Upgraded Version ESP-01,all Flash are upgraded to 1M byte.Also support Cloud service remote transmission.
