# Fritzing sketch Wifi (saved by Fritzing 0.9.3b)
breadboards: 1

parts:
  Componente1 = Arduino Uno (Rev3) - ICSP
  U1 = ESP8266 ESP-01 Upgraded WiFi Module [part_number=ESP8266]
  VCC2 = 4 x AAA Battery Mount

nets:
  N1: Componente1.D2, U1.RXD
  N2: Componente1.D3_PWM, U1.TXD
  3V3: Componente1.3V3, U1.VCC, U1.CH_PD, VCC2.+
  GND: Componente1.GND, U1.GND, VCC2.-

notes:
  URXD - GND
  CH_PD - GPIO2
  RST - GPIO0
  VCC - UTXD

custom parts:
  ESP8266 ESP-01 Upgraded WiFi Module: Upgraded Version ESP-01,all Flash are upgraded to 1M byte.Also support Cloud service remote transmission.
